// Logisim project 000_Decoder.circ as structural Verilog: 2 circuits, main circuit main
module main (
  input  x2,
  input  x1,
  input  e,
  input  x2_2,
  input  x1_2,
  input  Enable,
  input  [1:0] Input,
  input  [1:0] in_8,
  input  x0,
  input  x1_3,
  input  e_2,
  output y1,
  output y1_2,
  output y2,
  output y2_2,
  output y3,
  output y3_2,
  output y4,
  output y4_2,
  output [3:0] out_20,
  output [3:0] Output,
  output out_22,
  output out_23,
  output out_24,
  output out_25
);

  wire not_1_out, not_2_out, not_3_out, not_4_out, not_5_out, not_6_out;

  not not_1 (not_1_out, x2);
  not not_2 (not_2_out, x1);
  and and_1 (out_20[0], not_4_out, not_3_out);
  and and_2 (out_20[1], not_4_out, in_8[0]);
  and and_3 (out_20[2], in_8[1], not_3_out);
  and and_4 (out_20[3], in_8[1], in_8[0]);
  not not_3 (not_3_out, in_8[0]);
  not not_4 (not_4_out, in_8[1]);
  and and_5 (y1, not_1_out, not_2_out);
  and and_6 (y2, not_1_out, x1);
  and and_7 (y3, x2, not_2_out);
  and and_8 (y4, x2, x1);
  not not_5 (not_5_out, x2_2);
  and and_9 (y1_2, not_5_out, e, not_6_out);
  and and_10 (y2_2, not_5_out, e, x1_2);
  and and_11 (y3_2, x2_2, e, not_6_out);
  and and_12 (y4_2, x2_2, e, x1_2);
  not not_6 (not_6_out, x1_2);
  Decoder #(.select(2)) decoder_1 (
    .out0(Output[0]), .out1(Output[1]), .out2(Output[2]), .out3(Output[3]), .sel(Input), .en(Enable));
  _2_bit_Decoder u_2_bit_decoder_1 (.x1(x0), .x2(x1_3), .e(e_2), .y1(out_22), .y2(out_23), .y3(out_24), .y4(out_25));

  // Notes on the sheet:
  //   2-bit Decoder
  //   Using a Bus
  //   Individual Inputs
  //   y1=(x1)' * (x2)'
  //   y2=x1 * (x2)'
  //   y3=(x1)' * x2
  //   y4=x1 * x2
  //   Decoder: (Binary-Enoding) -> (One-Hot-Encoding)
  //   with Enable
  //   LogiSims Decoder
  //   Custom Sub-Circuit
  //   y1=(x1)' * (x2)'
  //   y2=x1 * (x2)'
  //   y3=(x1)' * x2
  //   y4=x1 * x2
endmodule

module _2_bit_Decoder (
  input  x1,
  input  x2,
  input  e,
  output y1,
  output y2,
  output y3,
  output y4
);

  wire not_1_out, not_2_out;

  and and_1 (y1, not_2_out, e, not_1_out);
  and and_2 (y2, not_2_out, e, x1);
  and and_3 (y3, x2, e, not_1_out);
  and and_4 (y4, x2, e, x1);
  not not_1 (not_1_out, x1);
  not not_2 (not_2_out, x2);

  // Notes on the sheet:
  //   y2=x1 * (x2)'
  //   y3=(x1)' * x2
  //   y4=x1 * x2
  //   y1=(x1)' * (x2)'
endmodule
