// Logisim project 000_Decoder_and_MUX.circ as structural Verilog: 2 circuits, main circuit main
module main (
  input  in_1,
  input  in_2,
  input  i0,
  input  in_4,
  input  i1,
  input  in_6,
  input  x2,
  input  x1,
  input  s,
  input  in_10,
  input  in_11,
  input  [1:0] in_12,
  input  s_2,
  input  [1:0] in_14,
  input  in_15,
  input  in_16,
  input  in_17,
  output y1,
  output y2,
  output y3,
  output out_21,
  output out_22,
  output y4,
  output [3:0] out_24,
  output out_25,
  output out_26,
  output out_27,
  output out_28
);

  wire and_9_out, and_10_out, and_11_out, and_12_out, and_13_out, and_14_out, and_15_out, and_16_out,
       clock_1_out, not_1_out, not_2_out, not_3_out, not_4_out, not_5_out, not_6_out, not_7_out, not_8_out;

  Clock clock_1 (.out(clock_1_out));
  not not_1 (not_1_out, x2);
  not not_2 (not_2_out, x1);
  and and_1 (out_24[0], not_4_out, not_3_out);
  and and_2 (out_24[1], not_4_out, in_14[0]);
  and and_3 (out_24[2], in_14[1], not_3_out);
  and and_4 (out_24[3], in_14[1], in_14[0]);
  not not_3 (not_3_out, in_14[0]);
  not not_4 (not_4_out, in_14[1]);
  D_Flip_Flop d_ff_1 (.clk(in_15), .D(in_16), .Q(out_26));  // open: Qn, preset, en, reset
  D_Flip_Flop d_ff_2 (.clk(clock_1_out), .D(in_17), .Q(out_27));  // open: Qn, preset, en, reset
  and and_5 (y1, not_1_out, not_2_out);
  and and_6 (y2, not_1_out, x1);
  and and_7 (y3, x2, not_2_out);
  and and_8 (y4, x2, x1);
  D_Flip_Flop d_ff_3 (.clk(clock_1_out), .D(in_17), .Q(out_28));  // open: Qn, preset, en, reset
  and and_9 (and_9_out, i0, not_5_out);
  and and_10 (and_10_out, i1, s);
  not not_5 (not_5_out, s);
  and and_11 (and_11_out, in_12[0], not_6_out);
  and and_12 (and_12_out, in_12[1], s_2);
  not not_6 (not_6_out, s_2);
  or or_1 (out_22, and_9_out, and_10_out);
  or or_2 (out_25, and_11_out, and_12_out);
  not not_7 (not_7_out, in_10);
  not not_8 (not_8_out, in_11);
  and and_13 (and_13_out, in_1, not_7_out, not_8_out);
  and and_14 (and_14_out, in_2, not_7_out, in_11);
  and and_15 (and_15_out, in_4, in_10, not_8_out);
  and and_16 (and_16_out, in_6, in_10, in_11);
  or or_3 (out_21, and_13_out, and_14_out, and_15_out, and_16_out);

  // Notes on the sheet:
  //   2-bit Decoder
  //   Using a Bus and Spitter
  //   Individual Inputs
  //   y1=(x1)' * (x2)'
  //   y2=x1 * (x2)'
  //   y3=(x1)' * x2
  //   y4=x1 * x2
  //   d=[i0 * (s0)'] + [i1 * s0]
  //   4x1 MUX
endmodule

module _2_bit_Decoder (
  input  x1,
  input  x2,
  output y1,
  output y2,
  output y3,
  output y4
);

  wire not_1_out, not_2_out, not_3_out, not_4_out;

  not not_1 (not_1_out, x1);
  not not_2 (not_2_out, x2);
  not not_3 (not_3_out, x1);
  not not_4 (not_4_out, x2);
  and and_1 (y4, x1, x2);
  and and_2 (y1, not_1_out, not_2_out);
  and and_3 (y2, not_3_out, x2);
  and and_4 (y3, x1, not_4_out);
endmodule
