// Logisim project 001_MUX.circ as structural Verilog: 2 circuits, main circuit main
module main (
  input  i0,
  input  i1,
  input  i0_2,
  input  i2,
  input  i1_2,
  input  i3,
  input  s,
  input  s1,
  input  s0,
  input  [3:0] in_10,
  input  [1:0] in_11,
  input  s_2,
  input  [1:0] in_13,
  output out_14,
  output out_15,
  output out_16,
  output out_17
);

  wire and_1_out, and_2_out, and_3_out, and_4_out, and_5_out, and_6_out, and_7_out, and_8_out, and_9_out,
       and_10_out, and_11_out, and_12_out, not_1_out, not_2_out, not_3_out, not_4_out, not_5_out, not_6_out;

  not not_1 (not_1_out, s);
  and and_1 (and_1_out, in_11[0], not_2_out);
  and and_2 (and_2_out, in_11[1], s_2);
  not not_2 (not_2_out, s_2);
  and and_3 (and_3_out, i0_2, not_1_out);
  or or_1 (out_15, and_3_out, and_4_out);
  and and_4 (and_4_out, i1_2, s);
  or or_2 (out_17, and_1_out, and_2_out);
  not not_3 (not_3_out, s1);
  not not_4 (not_4_out, in_13[1]);
  and and_5 (and_5_out, i0, not_3_out, not_5_out);
  and and_6 (and_6_out, i1, not_3_out, s0);
  and and_7 (and_7_out, i2, s1, not_5_out);
  and and_8 (and_8_out, i3, s1, s0);
  not not_5 (not_5_out, s0);
  and and_9 (and_9_out, in_10[0], not_4_out, not_6_out);
  and and_10 (and_10_out, in_10[1], not_4_out, in_13[0]);
  and and_11 (and_11_out, in_10[2], in_13[1], not_6_out);
  and and_12 (and_12_out, in_10[3], in_13[1], in_13[0]);
  not not_6 (not_6_out, in_13[0]);
  or or_3 (out_14, and_5_out, and_6_out, and_7_out, and_8_out);
  or or_4 (out_16, and_9_out, and_10_out, and_11_out, and_12_out);

  // Notes on the sheet:
  //   2x1 MUX
  //   Individual Inputs
  //   d=[i0 * (s0)'] + [i1 * s0]
  //   Using a Bus and Spitter
  //   4x1 MUX
endmodule

module _2_bit_Decoder (
  input  x1,
  input  x2,
  output y1,
  output y2,
  output y3,
  output y4
);

  wire not_1_out, not_2_out, not_3_out, not_4_out;

  not not_1 (not_1_out, x1);
  not not_2 (not_2_out, x2);
  not not_3 (not_3_out, x1);
  not not_4 (not_4_out, x2);
  and and_1 (y4, x1, x2);
  and and_2 (y1, not_1_out, not_2_out);
  and and_3 (y2, not_3_out, x2);
  and and_4 (y3, x1, not_4_out);
endmodule
