// Logisim project 200_Register_Parallel-Load.circ as structural Verilog: 4 circuits, main circuit main
module main (
  input  in_1,
  input  in_2,
  input  in_3,
  input  in_4,
  input  in_5,
  input  in_6,
  input  in_7,
  input  in_8,
  input  in_9,
  input  in_10,
  input  in_11,
  input  in_12,
  input  in_13,
  input  in_14,
  input  in_15,
  input  in_16,
  input  in_17,
  input  [1:0] in_18,
  input  in_19,
  output out_20,
  output out_21,
  output out_22,
  output out_23,
  output out_24,
  output out_25,
  output out_26,
  output out_27,
  output out_28,
  output out_29,
  output [1:0] out_30
);

  wire clock_1_out, clock_2_out, clock_3_out, clock_4_out, multiplexer_1_out, multiplexer_2_out,
       n2x1_mux_1_d, n2x1_mux_2_d, n2x1_mux_4_d, n2x1_mux_5_d, n2x1_mux_6_d, n2x1_mux_7_d, not_1_out,
       not_2_out;

  not not_1 (not_1_out, in_14);
  Clock clock_1 (.out(clock_1_out));
  _2x1_MUX u_2x1_mux_1 (.i0(out_25), .i1(in_5), .d(n2x1_mux_1_d), .s(in_10));
  Clock clock_2 (.out(clock_2_out));
  Multiplexer multiplexer_1 (.in0(in_12), .in1(out_28), .out(multiplexer_1_out), .sel(not_1_out), .en(1'b1));
  Clock clock_3 (.out(clock_3_out));
  _2x1_MUX u_2x1_mux_2 (.i0(out_26), .i1(in_6), .d(n2x1_mux_2_d), .s(in_10));
  D_Flip_Flop d_ff_1 (.clk(clock_2_out), .D(n2x1_mux_1_d), .Q(out_25));  // open: Qn, preset, en, reset
  Multiplexer multiplexer_2 (.in0(in_13), .in1(out_29), .out(multiplexer_2_out), .sel(not_1_out), .en(1'b1));
  D_Flip_Flop d_ff_2 (.clk(clock_1_out), .D(multiplexer_1_out), .Q(out_28));  // open: Qn, preset, en, reset
  _2_bit_Parallel_Load_Reg u_2_bit_parallel_load_reg_1 (
    .load(in_19), .clk(clock_3_out), .i1(in_18[1]), .i0(in_18[0]), .q1(out_30[1]), .q0(out_30[0]));
  D_Flip_Flop d_ff_3 (.clk(clock_2_out), .D(n2x1_mux_2_d), .Q(out_26));  // open: Qn, preset, en, reset
  D_Flip_Flop d_ff_4 (.clk(clock_1_out), .D(multiplexer_2_out), .Q(out_29));  // open: Qn, preset, en, reset
  not not_2 (not_2_out, in_17);
  Multiplexer multiplexer_3 (.in0(in_15), .in1(in_16), .out(out_27), .sel(not_2_out), .en(1'b1));
  _2x1_MUX u_2x1_mux_3 (.i0(in_8), .i1(in_7), .d(out_20), .s(in_11));
  Clock clock_4 (.out(clock_4_out));
  _2x1_MUX u_2x1_mux_4 (.i0(out_21), .i1(in_1), .d(n2x1_mux_4_d), .s(in_9));
  D_Flip_Flop d_ff_5 (.clk(clock_4_out), .D(n2x1_mux_4_d), .Q(out_21));  // open: Qn, preset, en, reset
  _2x1_MUX u_2x1_mux_5 (.i0(out_22), .i1(in_2), .d(n2x1_mux_5_d), .s(in_9));
  D_Flip_Flop d_ff_6 (.clk(clock_4_out), .D(n2x1_mux_5_d), .Q(out_22));  // open: Qn, preset, en, reset
  _2x1_MUX u_2x1_mux_6 (.i0(out_23), .i1(in_3), .d(n2x1_mux_6_d), .s(in_9));
  D_Flip_Flop d_ff_7 (.clk(clock_4_out), .D(n2x1_mux_6_d), .Q(out_23));  // open: Qn, preset, en, reset
  _2x1_MUX u_2x1_mux_7 (.i0(out_24), .i1(in_4), .d(n2x1_mux_7_d), .s(in_9));
  D_Flip_Flop d_ff_8 (.clk(clock_4_out), .D(n2x1_mux_7_d), .Q(out_24));  // open: Qn, preset, en, reset

  // Notes on the sheet:
  //   2-bit Parallel-Load Register
  //   Using Custom 2x1 MUX
  //   4-bit Parallel-Load Register
endmodule

module _2x1_MUX (
  input  i0,
  input  i1,
  input  s,
  output d
);

  wire and_1_out, and_2_out, not_1_out;

  not not_1 (not_1_out, s);
  and and_1 (and_1_out, i0, not_1_out);
  and and_2 (and_2_out, i1, s);
  or or_1 (d, and_1_out, and_2_out);

  // Notes on the sheet:
  //   d=[i0 * (s0)'] + [i1 * s0]
endmodule

module _4x1_MUX (
  input  i0,
  input  i1,
  input  i2,
  input  i3,
  input  s1,
  input  s0,
  output d
);

  wire and_1_out, and_2_out, and_3_out, and_4_out, not_1_out, not_2_out;

  not not_1 (not_1_out, s1);
  and and_1 (and_1_out, i0, not_1_out, not_2_out);
  and and_2 (and_2_out, i1, not_1_out, s0);
  and and_3 (and_3_out, i2, s1, not_2_out);
  and and_4 (and_4_out, i3, s1, s0);
  not not_2 (not_2_out, s0);
  or or_1 (d, and_1_out, and_2_out, and_3_out, and_4_out);
endmodule

module _2_bit_Parallel_Load_Reg (
  input  i1,
  input  i0,
  input  load,
  input  clk,
  output q1,
  output q0
);

  wire n2x1_mux_1_p2, n2x1_mux_2_p3;

  // _2x1_MUX 2x1_mux_1: pin names not known; wires that end beside it: i1, n2x1_mux_1_p2, load
  // _2x1_MUX 2x1_mux_2: pin names not known; wires that end beside it: load, i0, n2x1_mux_2_p3, q0
  D_Flip_Flop d_ff_1 (.clk(clk), .D(n2x1_mux_1_p2), .Q(load));  // open: Qn, preset, en, reset
  D_Flip_Flop d_ff_2 (.clk(clk), .D(n2x1_mux_2_p3), .Q(q0));  // open: Qn, preset, en, reset

  assign q1 = load;

  // Notes on the sheet:
  //   2-bit Parallel-Load Register
endmodule
