// Logisim project 300_Registe-File.circ as structural Verilog: 7 circuits, main circuit main
module _2x1_MUX (
  input  i0,
  input  i1,
  input  s,
  output d
);

  wire and_1_out, and_2_out, not_1_out;

  not not_1 (not_1_out, s);
  and and_1 (and_1_out, i0, not_1_out);
  and and_2 (and_2_out, i1, s);
  or or_1 (d, and_1_out, and_2_out);

  // Notes on the sheet:
  //   d=[i0 * (s0)'] + [i1 * s0]
endmodule

module _4x1_MUX (
  input  i0,
  input  i1,
  input  i2,
  input  i3,
  input  s1,
  input  s0,
  output d
);

  wire and_1_out, and_2_out, and_3_out, and_4_out, not_1_out, not_2_out;

  not not_1 (not_1_out, s1);
  and and_1 (and_1_out, i0, not_1_out, not_2_out);
  and and_2 (and_2_out, i1, not_1_out, s0);
  and and_3 (and_3_out, i2, s1, not_2_out);
  and and_4 (and_4_out, i3, s1, s0);
  not not_2 (not_2_out, s0);
  or or_1 (d, and_1_out, and_2_out, and_3_out, and_4_out);
endmodule

module main (
  input  [7:0] Input,
  input  in_2,
  input  Enable,
  input  [1:0] Input_2,
  output [7:0] Output,
  output [7:0] Output_2,
  output [3:0] Output_3,
  output [3:0] Output_4
);

  wire clock_1_out, not_1_out;

  Clock clock_1 (.out(clock_1_out));
  Register register_1 (.D(Input), .Q(Output), .clk(clock_1_out), .clr(not_1_out));  // open: en
  not not_1 (not_1_out, in_2);
  _8_bit_reg u_8_bit_reg_1 (.\input (Input), .clk(clock_1_out), .\output (Output_2), .load(in_2));
  Decoder #(.select(2)) decoder_1 (
    .out0(Output_3[0]), .out1(Output_3[1]), .out2(Output_3[2]), .out3(Output_3[3]), .sel(Input_2), .en(Enable));
  _2x4_decoder u_2x4_decoder_1 (
    .Enable(Enable), .Input(Input_2), .d0(Output_4[0]), .d1(Output_4[1]), .d2(Output_4[2]), .d3(Output_4[3]));

  // Notes on the sheet:
  //   4x4 register-file (<num-addresses>x<data-bits>)
endmodule

module _2_bit_Parallel_Load_Reg (
  input  i1,
  input  i0,
  input  load,
  input  clk,
  output q1,
  output q0
);

  wire multiplexer_1_out, multiplexer_2_out, not_1_out;

  not not_1 (not_1_out, load);
  Multiplexer multiplexer_1 (.in0(i1), .in1(q1), .out(multiplexer_1_out), .sel(not_1_out), .en(1'b1));
  Multiplexer multiplexer_2 (.in0(i0), .in1(q0), .out(multiplexer_2_out), .sel(not_1_out), .en(1'b1));
  D_Flip_Flop d_ff_1 (.clk(clk), .D(multiplexer_1_out), .Q(q1));  // open: Qn, preset, en, reset
  D_Flip_Flop d_ff_2 (.clk(clk), .D(multiplexer_2_out), .Q(q0));  // open: Qn, preset, en, reset

  // Notes on the sheet:
  //   2-bit Parallel-Load Register
endmodule

module _4_bit_Parallel_Load_Reg (
  input  i3,
  input  i2,
  input  i1,
  input  i0,
  input  load,
  input  clk,
  output q3,
  output q2,
  output q1,
  output q0
);

  wire multiplexer_1_out, multiplexer_2_out, multiplexer_3_out, multiplexer_4_out, not_1_out;

  not not_1 (not_1_out, load);
  Multiplexer multiplexer_1 (.in0(i3), .in1(q3), .out(multiplexer_1_out), .sel(not_1_out), .en(1'b1));
  Multiplexer multiplexer_2 (.in0(i2), .in1(q2), .out(multiplexer_2_out), .sel(not_1_out), .en(1'b1));
  D_Flip_Flop d_ff_1 (.clk(clk), .D(multiplexer_1_out), .Q(q3));  // open: Qn, preset, en, reset
  Multiplexer multiplexer_3 (.in0(i1), .in1(q1), .out(multiplexer_3_out), .sel(not_1_out), .en(1'b1));
  D_Flip_Flop d_ff_2 (.clk(clk), .D(multiplexer_2_out), .Q(q2));  // open: Qn, preset, en, reset
  Multiplexer multiplexer_4 (.in0(i0), .in1(q0), .out(multiplexer_4_out), .sel(not_1_out), .en(1'b1));
  D_Flip_Flop d_ff_3 (.clk(clk), .D(multiplexer_3_out), .Q(q1));  // open: Qn, preset, en, reset
  D_Flip_Flop d_ff_4 (.clk(clk), .D(multiplexer_4_out), .Q(q0));  // open: Qn, preset, en, reset

  // Notes on the sheet:
  //   4-bit Parallel-Load Register
endmodule

module _2x4_decoder (
  input  Enable,
  input  [1:0] Input,
  output d0,
  output d1,
  output d2,
  output d3
);

  Decoder #(.select(2)) decoder_1 (.out0(d0), .out1(d1), .out2(d2), .out3(d3), .sel(Input), .en(Enable));
endmodule

module _8_bit_reg (
  input  [7:0] \input ,
  input  clk,
  input  load,
  output [7:0] \output 
);

  wire not_1_out;

  Register register_1 (.D(\input ), .Q(\output ), .clk(clk), .clr(not_1_out));  // open: en
  not not_1 (not_1_out, load);
endmodule
