// Logisim project 302_RAM.circ as structural Verilog: 1 circuit, main circuit main
module main (
  input  [7:0] Store_Data,
  input  in_2,
  input  [7:0] Address,
  input  in_4,
  input  [3:0] Address_2,
  output [7:0] out_6,
  output [1:0] out_7,
  output [3:0] out_8
);

  wire clock_1_out, clock_2_out, not_1_out;
  wire [1:0] register_1_q;

  Clock clock_1 (.out(clock_1_out));
  Clock clock_2 (.out(clock_2_out));
  Register #(.width(1)) register_1 (.D(clock_1_out), .Q(register_1_q[0]));  // open: en, clk, clr
  assign out_6 = in_2 ? Store_Data : 8'bz;  // Controlled_Buffer controlled_buffer_1
  not not_1 (not_1_out, in_2);
  ROM #(.addrWidth(2), .dataWidth(2)) rom_1 (.addr(register_1_q), .data(out_7), .sel(in_4));
  ROM #(.addrWidth(4), .dataWidth(4)) rom_2 (.addr(Address_2), .data(out_8));  // open: sel
  RAM ram_1 (.addr(Address), .data(out_6), .clk(clock_2_out), .ld(not_1_out));  // open: sel, clr
  // Pins of 1 and 2 bits meet at register_1_q

  // Notes on the sheet:
  //   contents of rom_1 (hex, n*v repeats v):
  //   1 2 3 1
endmodule
