// Logisim project CPU.circ as structural Verilog: 9 circuits, main circuit main
module main (
  input  in_1,
  input  in_2,
  output [31:0] out_3,
  output Signed_OverFlow,
  output equal,
  output out_6,
  output [31:0] out_7
);

  wire MemWr;
  wire [4:0] instruction_memory_1_instr_15_11, instruction_memory_1_instr_20_16,
       instruction_memory_1_instr_25_21, mux_reg_file_1_zero_or_one, register_file_debug_1_write_reg_debug;
  wire [5:0] instruction_memory_1_instr_5_0;
  wire [15:0] instruction_memory_1_instr_15_0;
  wire [23:0] memory_data_1_address_2, memory_data_temp_1_address;
  wire [31:0] adder_1_out_3, alu_1_result, four_1_four, program_counter_1_pc, ra, register_file_debug_1_ra,
       register_file_debug_1_read_data_1, register_file_debug_1_read_data_2, register_file_debug_1_s1,
       register_file_debug_1_s2, register_file_debug_1_sp, s0, s1, s2, sign_extend_1_out_2, sp, write_data;

  // Probe on s0
  four four_1 (.four(four_1_four));
  program_counter program_counter_1 (.PC(program_counter_1_pc));
  // Probe on program_counter_1_pc
  // Probe on s1
  Adder adder_1 (.in_1(program_counter_1_pc), .in_2(four_1_four), .out_3(adder_1_out_3));
  // Probe on s2
  Instruction_Memory instruction_memory_1 (
    .Read_Address(program_counter_1_pc), .Instr_25_21(instruction_memory_1_instr_25_21),
    .Instr_20_16(instruction_memory_1_instr_20_16), .Instr_15_11(instruction_memory_1_instr_15_11),
    .Instr_15_0(instruction_memory_1_instr_15_0), .Instr_5_0(instruction_memory_1_instr_5_0));
  // Probe on ra
  // Probe on sp
  // Probe on instruction_memory_1_instr_20_16
  // Probe on instruction_memory_1_instr_25_21
  // Probe on instruction_memory_1_instr_15_0
  Debug debug_1 (
    .s0_out(s0), .s1_out(s1), .s2_out(s2), .ra_out(ra), .sp_out(sp), .s0(out_3),
    .s1(register_file_debug_1_s1), .s2(register_file_debug_1_s2), .ra(register_file_debug_1_ra),
    .sp(register_file_debug_1_sp));
  MUX_Reg_File mux_reg_file_1 (
    .Zero(instruction_memory_1_instr_20_16), .One(instruction_memory_1_instr_15_11),
    .Zero_or_One(mux_reg_file_1_zero_or_one), .Control(in_2));
  Sign_Extend sign_extend_1 (.in_1(instruction_memory_1_instr_15_0), .out_2(sign_extend_1_out_2));
  // Probe on write_data
  Register_File_DEBUG register_file_debug_1 (
    .Read_Register_1(instruction_memory_1_instr_25_21), .Read_Register_2(instruction_memory_1_instr_20_16),
    .Write_Register(mux_reg_file_1_zero_or_one), .Read_Data_1(register_file_debug_1_read_data_1),
    .Read_Data_2(register_file_debug_1_read_data_2), .s0(out_3), .s1(register_file_debug_1_s1),
    .s2(register_file_debug_1_s2), .ra(register_file_debug_1_ra), .sp(register_file_debug_1_sp),
    .Write_Data(write_data), .RegWrite(1'b1), .clk(in_1),
    .write_reg_DEBUG(register_file_debug_1_write_reg_debug), .MUX_output_16(out_6), .regs_output_16(out_7));
  // Probe on register_file_debug_1_write_reg_debug
  // Probe on register_file_debug_1_read_data_1
  // Probe on sign_extend_1_out_2
  alu alu_1 (
    .Switch(4'b0101), .X(register_file_debug_1_read_data_1), .Equal(equal), .Result(alu_1_result),
    .Signed_Overflow_18670403(Signed_OverFlow), .Y(sign_extend_1_out_2));
  // Probe on alu_1_result
  // Probe on memory_data_1_address_2
  // Probe on memory_data_temp_1_address
  memory_data memory_data_1 (
    .Address(alu_1_result), .Write_Data(register_file_debug_1_read_data_2), .in_2(in_1), .in_3(MemWr),
    .address_2(memory_data_1_address_2));  // open: Read_Data
  memory_data_temp memory_data_temp_1 (
    .instruction(write_data), .fetch_addr(alu_1_result), .address(memory_data_temp_1_address));
  // Probe on write_data

  // Other names for the same wires on the sheet: clk = in_1; RegDst = in_2

  // Notes on the sheet:
  //   rs
  //   rt
  //   -> ALU-Control
  //   ALU-Control (5=Add)
  //   Address
  //   Write-Data
endmodule

module Decode (
  input  [31:0] Instruction,
  output [5:0] opcode,
  output [4:0] RR1,
  output [4:0] RR2,
  output [15:0] out_5,
  output [5:0] func,
  output [4:0] out_7
);


  assign func = Instruction[5:0];
  assign opcode = Instruction[31:26];
  assign out_5 = Instruction[15:0];
  assign out_7 = Instruction[15:11];
  assign RR1 = Instruction[25:21];
  assign RR2 = Instruction[20:16];

  // Notes on the sheet:
  //   [26:31]
  //   [21:25]
  //   [16:20]
  //   [0:15]
  //   [0:5]
  //   [11:15]
endmodule

module Sign_Extend (
  input  [15:0] in_1,
  output [31:0] out_2
);

  assign out_2 = {{16{in_1[15]}}, in_1};  // Bit_Extender bit_extender_1
endmodule

module Instruction_Memory (
  input  [31:0] Read_Address,
  output [4:0] Instr_25_21,
  output [4:0] Instr_20_16,
  output [4:0] Instr_15_11,
  output [15:0] Instr_15_0,
  output [5:0] Instr_5_0
);

  wire [31:0] instruction_memory_1_instruction;

  instruction_memory instruction_memory_1 (.instruction(instruction_memory_1_instruction), .fetch_addr(Read_Address));
  Decode decode_1 (
    .Instruction(instruction_memory_1_instruction), .RR1(Instr_25_21), .RR2(Instr_20_16), .out_5(Instr_15_0),
    .func(Instr_5_0), .out_7(Instr_15_11));  // open: opcode
endmodule

module Register_File (
  input  [4:0] Read_Register_1,
  input  [4:0] Read_Register_2,
  input  [4:0] Write_Register,
  input  clk,
  input  RegWrite,
  input  [31:0] Write_Data,
  output [31:0] s0,
  output [31:0] s1,
  output [31:0] s2,
  output [31:0] ra,
  output [31:0] sp,
  output [31:0] Read_Data_1,
  output [31:0] Read_Data_2
);

  regfile regfile_1 (
    .read_reg1(Read_Register_1), .read_reg2(Read_Register_2), .write_register(Write_Register),
    .Data(Write_Data), .write_enable(RegWrite), .clock(clk), .read_data1(Read_Data_1),
    .read_data2(Read_Data_2), .reg_16_val(s0), .reg_17_val(s1), .reg_18_val(s2), .reg_19_val(ra),
    .reg_20_val(sp));
endmodule

module MUX_Reg_File (
  input  [4:0] Zero,
  input  [4:0] One,
  input  Control,
  output [4:0] Zero_or_One
);

  Multiplexer #(.width(5), .enable("false")) multiplexer_1 (.in0(Zero), .in1(One), .out(Zero_or_One), .sel(Control));
endmodule

module four (
  output [31:0] four
);


  assign four = 32'h4;
endmodule

module Debug (
  input  [31:0] s0,
  input  [31:0] s1,
  input  [31:0] s2,
  input  [31:0] ra,
  input  [31:0] sp,
  output [31:0] s0_out,
  output [31:0] s1_out,
  output [31:0] s2_out,
  output [31:0] ra_out,
  output [31:0] sp_out
);


  assign ra_out = ra;
  assign s0_out = s0;
  assign s1_out = s1;
  assign s2_out = s2;
  assign sp_out = sp;
endmodule

module Register_File_DEBUG (
  input  [4:0] Read_Register_1,
  input  [4:0] Read_Register_2,
  input  [4:0] Write_Register,
  input  RegWrite,
  input  clk,
  input  [31:0] Write_Data,
  output [31:0] s0,
  output [31:0] s1,
  output [31:0] s2,
  output [31:0] ra,
  output [31:0] sp,
  output [31:0] Read_Data_1,
  output [31:0] Read_Data_2,
  output [4:0] write_reg_DEBUG,
  output MUX_output_16,
  output [31:0] regs_output_16
);

  wire demultiplexer_1_out1, demultiplexer_1_out2, demultiplexer_1_out3, demultiplexer_1_out4,
       demultiplexer_1_out5, demultiplexer_1_out6, demultiplexer_1_out7, demultiplexer_1_out8,
       demultiplexer_1_out9, demultiplexer_1_out10, demultiplexer_1_out11, demultiplexer_1_out12,
       demultiplexer_1_out13, demultiplexer_1_out14, demultiplexer_1_out15, reg00_on_off, undriven,
       undriven_2, undriven_3, undriven_4, undriven_5, undriven_6, undriven_7, undriven_8, undriven_9,
       undriven_10, undriven_11, undriven_12, undriven_13, undriven_14, undriven_15, undriven_16,
       undriven_17, undriven_18, undriven_19, undriven_20, undriven_21, undriven_22, undriven_23,
       undriven_24, undriven_25, undriven_26, undriven_27, undriven_28, undriven_29, undriven_30;
  wire [31:0] reg01_out, reg02_out, reg03_out, reg04_out, reg05_out, reg06_out, reg07_out, reg08_out,
       reg09_out, reg10_out, reg11_out, reg12_out, reg13_out, reg14_out, reg15_out, reg19_out, reg20_out,
       reg21_out, reg22_out, reg23_out, reg24_out, reg26_out, reg27_out, reg28_out, reg29_out, reg30_out,
       reg_1_q, reg_2_q, reg_3_q, reg_4_q, reg_5_q, reg_6_q, reg_7_q, reg_8_q, reg_9_q, reg_10_q, reg_11_q,
       reg_12_q, reg_13_q, reg_14_q, reg_15_q, reg_17_q, reg_18_q, reg_19_q, reg_20_q, reg_21_q, reg_22_q,
       reg_23_q, reg_24_q, reg_25_q, reg_26_q, reg_27_q, reg_28_q, reg_29_q, reg_30_q, reg_31_q;

  // regfile regfile_1: pin names not known
  Demultiplexer #(.select(5), .enable("false")) demultiplexer_1 (
    .out0(reg00_on_off), .out1(demultiplexer_1_out1), .out2(demultiplexer_1_out2),
    .out3(demultiplexer_1_out3), .out4(demultiplexer_1_out4), .out5(demultiplexer_1_out5),
    .out6(demultiplexer_1_out6), .out7(demultiplexer_1_out7), .out8(demultiplexer_1_out8),
    .out9(demultiplexer_1_out9), .out10(demultiplexer_1_out10), .out11(demultiplexer_1_out11),
    .out12(demultiplexer_1_out12), .out13(demultiplexer_1_out13), .out14(demultiplexer_1_out14),
    .out15(demultiplexer_1_out15), .out16(MUX_output_16), .in(RegWrite), .sel(Write_Register));  // open: out17, out18, out19, out20, out21, out22, out23, out24, out25, out26, out27, out28, out29, out30, out31
  \reg  reg_1 (.D(Write_Data), .reg_on_off(undriven), .Q(reg_1_q), .clk(clk));
  \reg  reg_2 (.D(Write_Data), .reg_on_off(undriven_2), .Q(reg_2_q), .clk(clk));
  \reg  reg_3 (.D(Write_Data), .reg_on_off(undriven_3), .Q(reg_3_q), .clk(clk));
  \reg  reg_4 (.D(Write_Data), .reg_on_off(undriven_4), .Q(reg_4_q), .clk(clk));
  \reg  reg_5 (.D(Write_Data), .reg_on_off(undriven_5), .Q(reg_5_q), .clk(clk));
  \reg  reg_6 (.D(Write_Data), .reg_on_off(undriven_6), .Q(reg_6_q), .clk(clk));
  \reg  reg_7 (.D(Write_Data), .reg_on_off(undriven_7), .Q(reg_7_q), .clk(clk));
  \reg  reg_8 (.D(Write_Data), .reg_on_off(undriven_8), .Q(reg_8_q), .clk(clk));
  \reg  reg_9 (.D(Write_Data), .reg_on_off(undriven_9), .Q(reg_9_q), .clk(clk));
  \reg  reg_10 (.D(Write_Data), .reg_on_off(undriven_10), .Q(reg_10_q), .clk(clk));
  \reg  reg_11 (.D(Write_Data), .reg_on_off(undriven_11), .Q(reg_11_q), .clk(clk));
  \reg  reg_12 (.D(Write_Data), .reg_on_off(undriven_12), .Q(reg_12_q), .clk(clk));
  \reg  reg_13 (.D(Write_Data), .reg_on_off(undriven_13), .Q(reg_13_q), .clk(clk));
  \reg  reg_14 (.D(Write_Data), .reg_on_off(undriven_14), .Q(reg_14_q), .clk(clk));
  \reg  reg_15 (.D(Write_Data), .reg_on_off(undriven_15), .Q(reg_15_q), .clk(clk));
  \reg  reg_16 (.D(Write_Data), .reg_on_off(MUX_output_16), .Q(regs_output_16), .clk(clk));
  \reg  reg_17 (.D(Write_Data), .reg_on_off(undriven_16), .Q(reg_17_q), .clk(clk));
  \reg  reg_18 (.D(Write_Data), .reg_on_off(undriven_17), .Q(reg_18_q), .clk(clk));
  \reg  reg_19 (.D(Write_Data), .reg_on_off(undriven_18), .Q(reg_19_q), .clk(clk));
  \reg  reg_20 (.D(Write_Data), .reg_on_off(undriven_19), .Q(reg_20_q), .clk(clk));
  \reg  reg_21 (.D(Write_Data), .reg_on_off(undriven_20), .Q(reg_21_q), .clk(clk));
  \reg  reg_22 (.D(Write_Data), .reg_on_off(undriven_21), .Q(reg_22_q), .clk(clk));
  \reg  reg_23 (.D(Write_Data), .reg_on_off(undriven_22), .Q(reg_23_q), .clk(clk));
  \reg  reg_24 (.D(Write_Data), .reg_on_off(undriven_23), .Q(reg_24_q), .clk(clk));
  \reg  reg_25 (.D(Write_Data), .reg_on_off(undriven_24), .Q(reg_25_q), .clk(clk));
  \reg  reg_26 (.D(Write_Data), .reg_on_off(undriven_25), .Q(reg_26_q), .clk(clk));
  \reg  reg_27 (.D(Write_Data), .reg_on_off(undriven_26), .Q(reg_27_q), .clk(clk));
  \reg  reg_28 (.D(Write_Data), .reg_on_off(undriven_27), .Q(reg_28_q), .clk(clk));
  \reg  reg_29 (.D(Write_Data), .reg_on_off(undriven_28), .Q(reg_29_q), .clk(clk));
  \reg  reg_30 (.D(Write_Data), .reg_on_off(undriven_29), .Q(reg_30_q), .clk(clk));
  \reg  reg_31 (.D(Write_Data), .reg_on_off(undriven_30), .Q(reg_31_q), .clk(clk));
  read_mux read_mux_1 (
    .reg01_out(reg01_out), .in_2(reg02_out), .in_3(reg03_out), .in_5(reg04_out), .in_6(reg05_out),
    .in_7(reg06_out), .in_8(reg07_out), .in_9(reg08_out), .in_10(reg09_out), .in_11(reg10_out),
    .in_12(reg11_out), .in_13(reg12_out), .in_14(reg13_out), .in_15(reg14_out), .in_16(reg15_out),
    .in_17(regs_output_16), .in_19(s1), .in_20(s2), .in_21(reg19_out), .in_22(reg20_out), .in_23(reg21_out),
    .in_24(reg22_out), .in_25(reg23_out), .in_26(reg24_out), .in_27(sp), .in_28(reg26_out),
    .in_29(reg27_out), .in_30(reg28_out), .in_31(reg29_out), .in_32(reg30_out), .in_33(ra),
    .read_data1(Read_Data_1), .read_reg1(Read_Register_1), .read_data2(Read_Data_2),
    .read_reg2(Read_Register_2));

  assign s0 = regs_output_16;
  assign write_reg_DEBUG = Write_Register;

  // Other names for the same wires on the sheet: R1[31:0] = Read_Data_1; R2[31:0] = Read_Data_2;
  //   read_reg1[4:0] = Read_Register_1; RR1[4:0] = Read_Register_1; read_reg2[4:0] = Read_Register_2;
  //   RR2[4:0] = Read_Register_2; reg16_out[31:0] = regs_output_16; reg17_out[31:0] = s1; reg18_out[31:0] = s2;
  //   reg25_out[31:0] = sp; reg31_out[31:0] = ra; WA[31:0] = Write_Data; WE = RegWrite; write_en = RegWrite;
  //   RW[4:0] = Write_Register; write_reg[4:0] = Write_Register

  // Notes on the sheet:
  //   RR1
  //   RR2
  //   RW
  //   WA
  //   WE
  //   ^
  //   Write
  //   $s0 Val
  //   Debug
  //   $s1 Val
  //   $s2 Val
  //   $ra Val
  //   $sp Val
  //   Read
  //   R1
  //   R2
endmodule
